# Fritzing sketch Sketch (saved by Fritzing 0.9.3b)
circuit board: 9.62937cm x 9.74082cm
breadboards: 1

parts:
  Arduino = Arduino Uno (Rev3)
  LCD-I2C = LCD1602-I2C
  Buzzer = Piezo Speaker
  LED = LED - 5mm [color="Red (633nm)" package="5 mm [THT]"]
  R1 = Resistor [tolerance=±5% resistance=220 package=THT]
  BTN-1 = Pushbutton [package="[THT]"]
  BTN-2 = Pushbutton [package="[THT]"]
  BTN-3 = Pushbutton [package="[THT]"]

nets:
  N1: Arduino.A4/SDA, LCD-I2C.SDA
  N2: Arduino.A5/SCL, LCD-I2C.SCL
  N3: Arduino.D8, BTN-1.Pin_1, BTN-1.Pin_2
  N4: Arduino.D9_PWM, BTN-2.Pin_1, BTN-2.Pin_2
  N5: Arduino.D10_PWM/SS, BTN-3.Pin_1, BTN-3.Pin_2
  N6: Arduino.D2, Buzzer.pin2
  N7: Arduino.D3_PWM, R1.Pin_0
  5V: Arduino.5V, LCD-I2C.VCC
  GND: Arduino.GND, LCD-I2C.GND, Buzzer.pin1, LED.cathode, BTN-1.Pin_3, BTN-1.Pin_4, BTN-2.Pin_3, BTN-2.Pin_4, BTN-3.Pin_3, BTN-3.Pin_4
  N8: LED.anode, R1.Pin_1

notes:
  Display lcd-i2c 16x2
  Btn 1
  Btn 2
  Btn 3

custom parts:
  LCD1602-I2C: A standard character display, usually with 2x16 characters. Comes in many colors with LCM1602 IIC attached.
